// Logisim project conveyor.circ as structural Verilog: 2 circuits, main circuit pipe
module pipe (
  input  clk,
  input  ar,
  input  \направление ,
  input  \скорость ,
  input  \захват ,
  output [3:0] \шина_изделий ,
  output [1:0] \положение ,
  output \инд__ост ,
  output \инд__заполн ,
  output \инд__захвата 
);

  wire and_1_out, and_2_out, decoder_2_out3, multiplexer_1_out, multiplexer_2_out, multiplexer_3_out,
       multiplexer_4_out, multiplexer_5_out, multiplexer_6_out, multiplexer_7_out, multiplexer_8_out,
       multiplexer_9_out, multiplexer_10_out, not_1_out, not_2_out, or_1_out, or_2_out, \режим_q ;
  wire [3:0] and_3_out, decoder_1_out3, not_3_out;

  Multiplexer #(.enable("false")) multiplexer_1 (
    .in0(\инд__захвата ), .in1(multiplexer_6_out), .out(multiplexer_1_out), .sel(\режим_q ));
  Multiplexer #(.enable("false")) multiplexer_2 (
    .in0(multiplexer_4_out), .in1(multiplexer_7_out), .out(multiplexer_2_out), .sel(\режим_q ));
  and and_1 (and_1_out, \захват , ~\режим_q );  // AND_Gate
  Multiplexer #(.enable("false")) multiplexer_3 (
    .in0(and_2_out), .in1(multiplexer_9_out), .out(multiplexer_3_out), .sel(\режим_q ));
  D_Flip_Flop \u_режим  (.clk(clk), .D(multiplexer_1_out), .Q(\режим_q ), .reset(ar));  // open: Qn, preset, en
  Multiplexer #(.enable("false")) multiplexer_4 (
    .in0(\инд__заполн ), .in1(multiplexer_8_out), .out(multiplexer_4_out), .sel(\инд__захвата ));
  Multiplexer #(.enable("false")) multiplexer_5 (
    .in0(\скорость ), .in1(multiplexer_10_out), .out(multiplexer_5_out), .sel(\режим_q ));
  or or_1 (or_1_out, ar, \режим_q );
  D_Flip_Flop \u_инд__заполн  (
    .clk(clk), .D(multiplexer_2_out), .Q(\инд__заполн ), .reset(ar));  // open: Qn, preset, en
  D_Flip_Flop \u_инд__захвата  (.Q(\инд__захвата ), .preset(and_1_out), .reset(or_1_out));  // open: clk, D, Qn, en
  and and_2 (and_2_out, ~\направление , \скорость );  // AND_Gate
  or or_2 (or_2_out, \инд__захвата , \режим_q );
  not not_1 (not_1_out, \инд__ост );
  D_Flip_Flop \u_инд__ост  (.Q(\инд__ост ), .preset(or_2_out), .reset(not_2_out));  // open: clk, D, Qn, en
  not not_2 (not_2_out, or_2_out);
  Decoder #(.select(2), .enable("false")) decoder_1 (
    .out0(decoder_1_out3[3]), .out1(decoder_1_out3[2]), .out2(decoder_1_out3[1]), .out3(decoder_1_out3[0]),
    .sel(\положение ));
  Counter #(.width(2), .max('h3), .ongoal("stay")) \u_положение  (
    .load(multiplexer_3_out), .count(multiplexer_5_out), .Q(\положение ), .clk(clk));  // open: D, carry, clr
  Decoder #(.select(2), .enable("false")) decoder_2 (
    .out3(decoder_2_out3), .sel(\положение ));  // open: out0, out1, out2
  Shift_Register #(.length(4)) \u_конвейер  (
    .shift(not_1_out), .in(1'b1), .clk(clk), .load(\инд__захвата ), .clr(ar), .d0(and_3_out[3]),
    .q0(\шина_изделий [3]), .d1(and_3_out[2]), .q1(\шина_изделий [2]), .d2(and_3_out[1]),
    .q2(\шина_изделий [1]), .d3(and_3_out[0]), .q3(\шина_изделий [0]));  // open: out
  // Probe on and_3_out
  assign and_3_out = \шина_изделий  & not_3_out;  // AND_Gate and_3, 4 bits wide
  assign not_3_out = ~decoder_1_out3;  // NOT_Gate not_3, 4 bits wide
  Multiplexer #(.enable("false")) multiplexer_6 (
    .in0(\режим_q ), .in1(1'b0), .out(multiplexer_6_out), .sel(decoder_2_out3));
  Multiplexer #(.enable("false")) multiplexer_7 (
    .in0(\инд__заполн ), .in1(1'b0), .out(multiplexer_7_out), .sel(decoder_2_out3));
  Multiplexer #(.select(2), .enable("false")) multiplexer_8 (
    .in0(\шина_изделий [3]), .in1(\шина_изделий [2]), .in2(\шина_изделий [1]), .in3(\шина_изделий [0]),
    .out(multiplexer_8_out), .sel(\положение ));
  Multiplexer #(.enable("false")) multiplexer_9 (.in0(1'b0), .in1(1'b0), .out(multiplexer_9_out), .sel(decoder_2_out3));
  Multiplexer #(.enable("false")) multiplexer_10 (
    .in0(1'b1), .in1(1'b0), .out(multiplexer_10_out), .sel(decoder_2_out3));

  // Notes on the sheet:
  //   выбор режима
  //   выбор инд. заполн.
  //   выбор загрузки в положении
  //   выбор счёта в положении
  //   выбор режима в авт.
  //   загрузка в положении а авт.
  //   выбор инд. заполн. в авт.
  //   счёт в положении в авт.
endmodule

module main (
  input  ar,
  input  \направление ,
  input  \скорость 
);

  wire clk_out, decoder_1_out0, decoder_1_out1, decoder_1_out2, decoder_1_out3, \pipe_1_инд__заполн ,
       \pipe_1_инд__захвата , \pipe_1_инд__ост , \захват_out ;
  wire [1:0] \pipe_1_положение ;
  wire [3:0] \pipe_1_шина_изделий ;
  wire [4:0] multiplexer_1_out, multiplexer_1_out_2, multiplexer_1_out_3, multiplexer_1_out_4,
       multiplexer_1_out_5, multiplexer_3_out, multiplexer_3_out_2, multiplexer_3_out_3, multiplexer_3_out_4,
       multiplexer_3_out_5, multiplexer_4_out, multiplexer_4_out_2, multiplexer_4_out_3, multiplexer_6_out,
       multiplexer_6_out_2, multiplexer_6_out_3, multiplexer_6_out_4, multiplexer_6_out_5, multiplexer_9_out,
       multiplexer_9_out_2, multiplexer_9_out_3, multiplexer_9_out_4, multiplexer_9_out_5;
  wire [24:0] multiplexer_2_out, multiplexer_5_out, multiplexer_7_out, multiplexer_8_out;
  wire [24:15] multiplexer_4_out_4;

  Clock clk (.out(clk_out));
  pipe pipe_1 (
    .ar(ar), .\направление (\направление ), .\скорость (\скорость ), .\захват (\захват_out ),
    .\шина_изделий (\pipe_1_шина_изделий ), .\инд__ост (\pipe_1_инд__ост ),
    .\инд__заполн (\pipe_1_инд__заполн ), .\инд__захвата (\pipe_1_инд__захвата ), .clk(clk_out),
    .\положение (\pipe_1_положение ));
  Button \u_захват  (.out(\захват_out ));
  Decoder #(.select(2), .disabled(0), .enable("false")) decoder_1 (
    .out0(decoder_1_out0), .out1(decoder_1_out1), .out2(decoder_1_out2), .out3(decoder_1_out3),
    .sel(\pipe_1_положение ));
  LED clk_2 (.in(clk_out));
  LED u_ar (.in(ar));
  DotMatrix #(.matrixrows(5)) dotmatrix_1 (
    .col0(multiplexer_1_out_5), .col1(multiplexer_1_out_4), .col2(multiplexer_1_out_3),
    .col3(multiplexer_1_out_2), .col4(multiplexer_1_out));
  LED led_1 (.in(\pipe_1_шина_изделий [3]));
  LED led_2 (.in(\pipe_1_шина_изделий [2]));
  DotMatrix #(.matrixrows(5)) dotmatrix_2 (
    .col0(multiplexer_3_out_5), .col1(multiplexer_3_out_4), .col2(multiplexer_3_out_3),
    .col3(multiplexer_3_out_2), .col4(multiplexer_3_out));
  Multiplexer #(.width(25), .enable("false")) multiplexer_1 (
    .in0({25{1'b0}}), .in1(multiplexer_2_out),
    .out({multiplexer_1_out_5, multiplexer_1_out_4, multiplexer_1_out_3, multiplexer_1_out_2, multiplexer_1_out}),
    .sel(decoder_1_out0));
  Multiplexer #(.width(25), .enable("false")) multiplexer_2 (
    .in0(25'h1f0843f), .in1(25'h1f0943f), .out(multiplexer_2_out), .sel(\pipe_1_инд__заполн ));
  LED led_3 (.in(\pipe_1_шина_изделий [1]));
  DotMatrix #(.matrixrows(5)) dotmatrix_3 (
    .col0(multiplexer_4_out_4[24:20]), .col1(multiplexer_4_out_4[19:15]), .col2(multiplexer_4_out_3),
    .col3(multiplexer_4_out_2), .col4(multiplexer_4_out));
  Multiplexer #(.width(25), .enable("false")) multiplexer_3 (
    .in0({25{1'b0}}), .in1(multiplexer_5_out),
    .out({multiplexer_3_out_5, multiplexer_3_out_4, multiplexer_3_out_3, multiplexer_3_out_2, multiplexer_3_out}),
    .sel(decoder_1_out1));
  Multiplexer #(.width(25), .enable("false")) multiplexer_4 (
    .in0({25{1'b0}}), .in1(multiplexer_8_out),
    .out({multiplexer_4_out_4, multiplexer_4_out_3, multiplexer_4_out_2, multiplexer_4_out}),
    .sel(decoder_1_out2));
  Multiplexer #(.width(25), .enable("false")) multiplexer_5 (
    .in0(25'h1f0843f), .in1(25'h1f0943f), .out(multiplexer_5_out), .sel(\pipe_1_инд__заполн ));
  LED led_4 (.in(\pipe_1_шина_изделий [0]));
  DotMatrix #(.matrixrows(5)) dotmatrix_4 (
    .col0(multiplexer_9_out_5), .col1(multiplexer_9_out_4), .col2(multiplexer_9_out_3),
    .col3(multiplexer_9_out_2), .col4(multiplexer_9_out));
  DotMatrix #(.matrixrows(5)) dotmatrix_5 (
    .col0(multiplexer_6_out_5), .col1(multiplexer_6_out_4), .col2(multiplexer_6_out_3),
    .col3(multiplexer_6_out_2), .col4(multiplexer_6_out));
  Multiplexer #(.width(25), .enable("false")) multiplexer_6 (
    .in0({25{1'b0}}), .in1(multiplexer_7_out),
    .out({multiplexer_6_out_5, multiplexer_6_out_4, multiplexer_6_out_3, multiplexer_6_out_2, multiplexer_6_out}),
    .sel(decoder_1_out3));
  Multiplexer #(.width(25), .enable("false")) multiplexer_7 (
    .in0(25'h1f0843f), .in1(25'h1f0943f), .out(multiplexer_7_out), .sel(\pipe_1_инд__заполн ));
  Multiplexer #(.width(25), .enable("false")) multiplexer_8 (
    .in0(25'h1f0843f), .in1(25'h1f0943f), .out(multiplexer_8_out), .sel(\pipe_1_инд__заполн ));
  LED \u_Индикатор_захвата  (.in(\pipe_1_инд__захвата ));
  Multiplexer #(.width(25), .enable("false")) multiplexer_9 (
    .in0(25'h4255c4), .in1({25{1'b0}}),
    .out({multiplexer_9_out_5, multiplexer_9_out_4, multiplexer_9_out_3, multiplexer_9_out_2, multiplexer_9_out}),
    .sel(\pipe_1_инд__ост ));

  // Notes on the sheet:
  //   ЗДЕСЬ ДОЛЖНА БЫТЬ ГЛАВНАЯ СХЕМА
  //   Выходы сверху вниз: шина изделий, положение лапы, индикатор остановки конвейера, индикатор заполненности лапы, индикатор захвата
  //   Шина изделий
  //   Положение и заполненность лапы
  //   Направление движения конвейера
endmodule
